# Fritzing sketch fritzing_diagram_clear_asteroids (saved by Fritzing 0.9.3b)
breadboards: 3

parts:
  Part1 = PocketBeagle
  Part2 = 0.56" 7-segment LED Backpack [part_number=878]
  Part3 = Thumb Joystick
  Part4 = TXB0108 8-channel Bi-directional Logic Level Converter
  Part5 = TXB0108 8-channel Bi-directional Logic Level Converter
  J1 = Piezo Speaker
  R1 = Resistor [tolerance=±5% resistance=100 package="2512 [SMD]"]
  R2 = Resistor [tolerance=±5% resistance=10k package="2512 [SMD]"]
  R3 = Resistor [tolerance=±5% resistance=10k package="2512 [SMD]"]
  R4 = Resistor [tolerance=±5% resistance=10k package="2512 [SMD]"]
  R5 = Resistor [tolerance=±5% resistance=10k package="2512 [SMD]"]
  R6 = Resistor [tolerance=±5% resistance=10k package="2512 [SMD]"]
  R7 = Resistor [tolerance=±5% resistance=10k package="2512 [SMD]"]
  R8 = Resistor [tolerance=±5% resistance=10k package="2512 [SMD]"]

nets:
  3.3V: Part1.3.3V, Part2.VDD, Part4.VCCB, Part5.VCCB, R1.Pin_1, R2.Pin_1, R3.Pin_1
  GND: Part1.GND, Part2.GND, Part4.GND, Part4.A8, Part4.A4, Part4.A2, Part5.GND, J1.pin1
  N1: Part1.AIN.VREFN, Part3.GND
  N2: Part1.AIN0(1.8V), R7.Pin_1, R8.Pin_0
  N3: Part1.VOUT, Part4.OE, Part4.VCCA, Part5.OE, Part5.VCCA
  N4: Part1.GPIO26, Part5.A4
  N5: Part1.PWM0A, J1.pin2, R1.Pin_0
  N6: Part1.PWM1A, Part5.A8
  N7: Part1.GPIO59, Part5.A1
  N8: Part1.GPIO23, Part5.A3
  N9: Part1.GPIO58, Part5.A2
  N10: Part1.GPIO57, Part4.A1
  N11: Part1.GPIO60, Part4.A7
  N12: Part1.I2C1.SCL, Part2.SCL, R2.Pin_0
  N13: Part1.GPIO52, Part5.A7
  N14: Part1.I2C1.SDA, Part2.SDA, R3.Pin_0
  N15: Part1.GPIO47, Part4.A6
  N16: Part1.GPIO46, Part5.A6
  N17: Part1.GPIO48, Part5.A5
  N18: Part3.SEL, R5.Pin_1
  N19: Part3.HORZ, R8.Pin_1
  N20: Part3.VERT, R6.Pin_1
  N21: Part3.VCC, R4.Pin_0, R5.Pin_0, R7.Pin_0
  N22: R4.Pin_1, R6.Pin_0

notes:
  Pseudo set-up of Adafruit 32x32 RGB Matrix.
  Row1, Left Pin - Green1
  Row2, Left Pin - GND
  Row3, Left Pin - Green 2
  Row4, Left Pin - GND
  Row5, Left Pin - B
  Row6, Left Pin - D
  Row7, Left Pin - Latch
  Row8, Left Pin - GND
  Row1, Right Pin - Red 1
  Row2, Right Pin - Blue 1
  Row3, Right Pin - Red 2
  Row4, Right Pin - Blue 2
  Row5, Right Pin - A
  Row6, Right Pin - C
  Row7, Right Pin - Clock
  Row8, Right Pin - Output En

custom parts:
  0.56" 7-segment LED Backpack: This 0.56" 7-segment LED display includes a driver chip for simple control via an I2C interface. The backpack features address-selection jumpers so you can connect up to eight displays on a single I2C bus.
  TXB0108 8-channel Bi-directional Logic Level Converter: Because the Arduino (and Basic Stamp) are 5V devices, and most modern sensors, displays, flash cards and modes are 3.3V-only, many makers find that they need to perform level shifting/conversion to protect the 3.3V device from 5V. Although one can use resistors to make a divider, for high speed transfers, the resistors can add a lot of slew and cause havoc that is tough to debug. For that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
